// Logisim project RiscV.circ as structural Verilog: 8 circuits, main circuit main
module main (
  input  in_1,
  input  in_2,
  input  in_3,
  input  in_4,
  input  in_5,
  input  in_6,
  input  [6:0] in_7
);

  wire ALUzero, and_1_out, button_1_out, clock_1_out, clock_2_out, clock_3_out, clock_4_out, not_1_out,
       not_2_out, not_3_out;
  wire [4:0] rom_1_data_2, rom_1_data_3, rom_1_data_4;
  wire [7:0] rom_2_data;
  wire [23:0] register_1_q;
  wire [31:0] adder_1_out, adder_2_out, ALUout, bancoregistradores_1_rs1, IMMext, multiplexer_1_out,
       multiplexer_2_out, multiplexer_3_out, RAMout, RAMrs2, rom_1_data;
  wire [31:24] register_1_q_2;

  Clock clock_1 (.out(clock_1_out));
  not not_1 (not_1_out, clock_1_out);
  ROM #(.addrWidth(24), .dataWidth(32)) rom_1 (
    .addr(register_1_q),
    .data({rom_1_data[31:25], rom_1_data_4, rom_1_data_3, rom_1_data[14:12], rom_1_data_2, rom_1_data[6:0]}));
  ROM #(.addrWidth(7)) rom_2 (.addr(in_7), .data(rom_2_data));
  Multiplexer #(.width(32)) multiplexer_1 (
    .in0(adder_1_out), .in1(adder_2_out), .out(multiplexer_1_out), .sel(and_1_out));
  Register #(.width(32)) register_1 (
    .D(multiplexer_1_out), .en(not_1_out), .clk(not_1_out), .Q({register_1_q_2, register_1_q}),
    .clr(button_1_out));
  Button button_1 (.out(button_1_out));
  and and_1 (and_1_out, ALUzero, in_6);
  Adder #(.width(32)) adder_1 (.a({register_1_q_2, register_1_q}), .b(32'h4), .out(adder_1_out));  // open: cin, cout
  Adder #(.width(32)) adder_2 (.a({register_1_q_2, register_1_q}), .b(IMMext), .out(adder_2_out));  // open: cin, cout
  // Probe on RAMout
  Clock clock_2 (.out(clock_2_out));
  // Probe on rom_1_data_2
  // Probe on rom_1_data_3
  // Probe on rom_1_data_4
  Register register_2 (.D(rom_2_data), .en(not_2_out), .clk(not_2_out));  // open: Q, clr
  not not_2 (not_2_out, clock_2_out);
  Multiplexer #(.width(32)) multiplexer_2 (.in0(ALUout), .in1(RAMout), .out(multiplexer_2_out), .sel(in_1));
  Clock clock_3 (.out(clock_3_out));
  not not_3 (not_3_out, clock_3_out);
  // Probe on {rom_1_data[31:25], rom_1_data_4, rom_1_data_3, rom_1_data[14:12], rom_1_data_2, rom_1_data[6:0]}
  // Probe on ALUout
  // Probe on IMMext
  bancoRegistradores bancoregistradores_1 (
    .clk(not_3_out), .rsi2(rom_1_data_4), .rdi(rom_1_data_2), .data(multiplexer_2_out), .WE(in_2),
    .rsi1(rom_1_data_3), .rs1(bancoregistradores_1_rs1), .rs2(RAMrs2));
  ImediatoGenerator imediatogenerator_1 (
    .OPCODE({rom_1_data[31:25], rom_1_data_4, rom_1_data_3, rom_1_data[14:12], rom_1_data_2, rom_1_data[6:0]}),
    .out_2(IMMext));
  // Probe on bancoregistradores_1_rs1
  // Probe on RAMrs2
  Multiplexer #(.width(32)) multiplexer_3 (.in0(RAMrs2), .in1(IMMext), .out(multiplexer_3_out), .sel(in_3));
  // Probe on multiplexer_3_out
  ULA ula_1 (
    .sel(4'b1111), .dataA(bancoregistradores_1_rs1), .dataB(multiplexer_3_out), .dataD(ALUout), .zero(ALUzero));
  // Probe on ALUout
  // Probe on ALUout[25:2]
  Clock clock_4 (.out(clock_4_out));
  // Probe on RAMrs2
  RAM #(.addrWidth(24), .dataWidth(32)) ram_1 (
    .addr(ALUout[25:2]), .we(in_4), .oe(in_5), .clk(clock_4_out), .din(RAMrs2), .dout(RAMout));
  // Probe on RAMout

  // Other names for the same wires on the sheet: ALUSrc = in_3; Branch = in_6; MemRead = in_5; MemtoReg = in_1;
  //   MemWrite = in_4; RegWrite = in_2

  // Notes on the sheet:
  //   contents of rom_1 (hex, n*v repeats v):
  //   a337
  //   contents of rom_2 (hex, n*v repeats v):
  //   20 c 6 30 52 14 70 a 20 c 26 30 52 c 60 a 20 c 46 30 51 54 60 a 20 c 66 30 51 60 64 a 20 d 46 30 51
  //   40 6a a 20 d 46 70 51 60 60 a 20 d 48 60 51 60 60
  //   addi x1,x0 5
  //   sw x1, 4(x0)
  //   lw x2, 4(x0)
  //   0110002
  //   0011002
  //   1110102
  //   endereco
endmodule

module bancoRegistradores (
  input  [4:0] rsi1,
  input  [4:0] rsi2,
  input  [4:0] rdi,
  input  [31:0] data,
  input  WE,
  input  clk,
  output [31:0] rs1,
  output [31:0] rs2
);

  wire x0we_t, x1we_t, x2we_t, x3we_t, x4we_t, x5we_t, x6we_t, x7we_t, x8we_t, x9we_t, x10we_t, x11we_t,
       x12we_t, x13we_t, x14we_t, x15we_t, x16we_t, x17we_t, x18we_t, x19we_t, x20we_t, x21we_t, x22we_t,
       x23we_t, x24we_t, x25we_t, x26we_t, x27we_t, x28we_t, x29we_t, x30we_t, x31we_t;
  wire [31:0] x1q_t, x2q_t, x3q_t, x4q_t, x5q_t, x6q_t, x7q_t, x8q_t, x9q_t, x10q_t, x11q_t, x12q_t, x13q_t,
       x14q_t, x15q_t, x16q_t, x17q_t, x18q_t, x19q_t, x20q_t, x21q_t, x22q_t, x23q_t, x24q_t, x25q_t,
       x26q_t, x27q_t, x28q_t, x29q_t, x30q_t, x31q_t;

  Demultiplexer #(.select(5)) demultiplexer_1 (
    .out0(x0we_t), .out1(x1we_t), .out2(x2we_t), .out3(x3we_t), .out4(x4we_t), .out5(x5we_t), .out6(x6we_t),
    .out7(x7we_t), .out8(x8we_t), .out9(x9we_t), .out10(x10we_t), .out11(x11we_t), .out12(x12we_t),
    .out13(x13we_t), .out14(x14we_t), .out15(x15we_t), .out16(x16we_t), .out17(x17we_t), .out18(x18we_t),
    .out19(x19we_t), .out20(x20we_t), .out21(x21we_t), .out22(x22we_t), .out23(x23we_t), .out24(x24we_t),
    .out25(x25we_t), .out26(x26we_t), .out27(x27we_t), .out28(x28we_t), .out29(x29we_t), .out30(x30we_t),
    .out31(x31we_t), .in(WE), .sel(rdi));
  Register #(.width(32)) x4 (.D(data), .en(x4we_t), .clk(clk), .Q(x4q_t));  // open: clr
  Register #(.width(32)) x8 (.D(data), .en(x8we_t), .clk(clk), .Q(x8q_t));  // open: clr
  Register #(.width(32)) x12 (.D(data), .en(x12we_t), .clk(clk), .Q(x12q_t));  // open: clr
  Register #(.width(32)) x16 (.D(data), .en(x16we_t), .clk(clk), .Q(x16q_t));  // open: clr
  Register #(.width(32)) x20 (.D(data), .en(x20we_t), .clk(clk), .Q(x20q_t));  // open: clr
  Register #(.width(32)) x24 (.D(data), .en(x24we_t), .clk(clk), .Q(x24q_t));  // open: clr
  Register #(.width(32)) x28 (.D(data), .en(x28we_t), .clk(clk), .Q(x28q_t));  // open: clr
  Register #(.width(32)) x1 (.D(data), .en(x1we_t), .clk(clk), .Q(x1q_t));  // open: clr
  Register #(.width(32)) x5 (.D(data), .en(x5we_t), .clk(clk), .Q(x5q_t));  // open: clr
  Register #(.width(32)) x9 (.D(data), .en(x9we_t), .clk(clk), .Q(x9q_t));  // open: clr
  Register #(.width(32)) x13 (.D(data), .en(x13we_t), .clk(clk), .Q(x13q_t));  // open: clr
  Register #(.width(32)) x17 (.D(data), .en(x17we_t), .clk(clk), .Q(x17q_t));  // open: clr
  Register #(.width(32)) x21 (.D(data), .en(x21we_t), .clk(clk), .Q(x21q_t));  // open: clr
  Register #(.width(32)) x25 (.D(data), .en(x25we_t), .clk(clk), .Q(x25q_t));  // open: clr
  Register #(.width(32)) x29 (.D(data), .en(x29we_t), .clk(clk), .Q(x29q_t));  // open: clr
  Register #(.width(32)) x2 (.D(data), .en(x2we_t), .clk(clk), .Q(x2q_t));  // open: clr
  Register #(.width(32)) x6 (.D(data), .en(x6we_t), .clk(clk), .Q(x6q_t));  // open: clr
  Register #(.width(32)) x10 (.D(data), .en(x10we_t), .clk(clk), .Q(x10q_t));  // open: clr
  Register #(.width(32)) x14 (.D(data), .en(x14we_t), .clk(clk), .Q(x14q_t));  // open: clr
  Register #(.width(32)) x18 (.D(data), .en(x18we_t), .clk(clk), .Q(x18q_t));  // open: clr
  Register #(.width(32)) x22 (.D(data), .en(x22we_t), .clk(clk), .Q(x22q_t));  // open: clr
  Register #(.width(32)) x26 (.D(data), .en(x26we_t), .clk(clk), .Q(x26q_t));  // open: clr
  Register #(.width(32)) x30 (.D(data), .en(x30we_t), .clk(clk), .Q(x30q_t));  // open: clr
  Register #(.width(32)) x3 (.D(data), .en(x3we_t), .clk(clk), .Q(x3q_t));  // open: clr
  Register #(.width(32)) x7 (.D(data), .en(x7we_t), .clk(clk), .Q(x7q_t));  // open: clr
  Register #(.width(32)) x11 (.D(data), .en(x11we_t), .clk(clk), .Q(x11q_t));  // open: clr
  Register #(.width(32)) x15 (.D(data), .en(x15we_t), .clk(clk), .Q(x15q_t));  // open: clr
  Register #(.width(32)) x19 (.D(data), .en(x19we_t), .clk(clk), .Q(x19q_t));  // open: clr
  Register #(.width(32)) x23 (.D(data), .en(x23we_t), .clk(clk), .Q(x23q_t));  // open: clr
  Register #(.width(32)) x27 (.D(data), .en(x27we_t), .clk(clk), .Q(x27q_t));  // open: clr
  Register #(.width(32)) x31 (.D(data), .en(x31we_t), .clk(clk), .Q(x31q_t));  // open: clr
  Multiplexer #(.select(5), .width(32)) multiplexer_1 (
    .in0({32{1'b0}}), .in1(x1q_t), .in2(x2q_t), .in3(x3q_t), .in4(x4q_t), .in5(x5q_t), .in6(x6q_t),
    .in7(x7q_t), .in8(x8q_t), .in9(x9q_t), .in10(x10q_t), .in11(x11q_t), .in12(x12q_t), .in13(x13q_t),
    .in14(x14q_t), .in15(x15q_t), .in16(x16q_t), .in17(x17q_t), .in18(x18q_t), .in19(x19q_t), .in20(x20q_t),
    .in21(x21q_t), .in22(x22q_t), .in23(x23q_t), .in24(x24q_t), .in25(x25q_t), .in26(x26q_t), .in27(x27q_t),
    .in28(x28q_t), .in29(x29q_t), .in30(x30q_t), .in31(x31q_t), .out(rs1), .sel(rsi1));
  Multiplexer #(.select(5), .width(32)) multiplexer_2 (
    .in0({32{1'b0}}), .in1(x1q_t), .in2(x2q_t), .in3(x3q_t), .in4(x4q_t), .in5(x5q_t), .in6(x6q_t),
    .in7(x7q_t), .in8(x8q_t), .in9(x9q_t), .in10(x10q_t), .in11(x11q_t), .in12(x12q_t), .in13(x13q_t),
    .in14(x14q_t), .in15(x15q_t), .in16(x16q_t), .in17(x17q_t), .in18(x18q_t), .in19(x19q_t), .in20(x20q_t),
    .in21(x21q_t), .in22(x22q_t), .in23(x23q_t), .in24(x24q_t), .in25(x25q_t), .in26(x26q_t), .in27(x27q_t),
    .in28(x28q_t), .in29(x29q_t), .in30(x30q_t), .in31(x31q_t), .out(rs2), .sel(rsi2));

  // Other names for the same wires on the sheet: clk_t = clk; rd_t[31:0] = data; rdi_t[4:0] = rdi; rs1_t[31:0] = rs1;
  //   rs2_t[31:0] = rs2; rsi1_t[4:0] = rsi1; rsi2_t[4:0] = rsi2; we_t = WE
endmodule

module ULA (
  input  [31:0] dataA,
  input  [31:0] dataB,
  input  [3:0] sel,
  output [31:0] dataD,
  output zero
);

  wire [31:0] adder_1_out, and_1_out, or_1_out, shifter_1_out, subtractor_1_out;

  assign and_1_out = dataA & dataB;  // AND_Gate and_1, 32 bits wide
  assign or_1_out = dataA | dataB;  // OR_Gate or_1, 32 bits wide
  Adder #(.width(32)) adder_1 (.a(dataA), .b(dataB), .out(adder_1_out));  // open: cin, cout
  Shifter #(.width(32)) shifter_1 (.in(dataA), .\dist (dataB[4:0]), .out(shifter_1_out));
  Subtractor #(.width(32)) subtractor_1 (.a(dataA), .b(dataB), .out(subtractor_1_out));  // open: bin, bout
  Multiplexer #(.select(4), .width(32)) multiplexer_1 (
    .in0(and_1_out), .in1(or_1_out), .in2(adder_1_out), .in3(shifter_1_out), .in4(dataB), .in5(dataB),
    .in6(subtractor_1_out), .in7(dataB), .in8(dataB), .in9(dataB), .in10(dataB), .in11(dataB), .in12(dataB),
    .in13(dataB), .in14(dataB), .in15(dataB), .out(dataD), .sel(sel));
  nor nor_1 (zero, dataD[0], dataD[1], dataD[2], dataD[3], dataD[4], dataD[5], dataD[6], dataD[7], dataD[8], dataD[9], dataD[10], dataD[11], dataD[12], dataD[13], dataD[14], dataD[15], dataD[16], dataD[17], dataD[18], dataD[19], dataD[20], dataD[21], dataD[22], dataD[23], dataD[24], dataD[25], dataD[26], dataD[27], dataD[28], dataD[29], dataD[30], dataD[31]);

  // Other names for the same wires on the sheet: dataA_t[31:0] = dataA; dataB_t[31:0] = dataB; dataD_t[31:0] = dataD;
  //   sel_t[3:0] = sel

  // Notes on the sheet:
  //   desloca no maximo 2 elevado a 5 menos 1
  //   0000 and
  //   0001 or
  //   0010 add
  //   0110 sub
  //   0011 sll
  //   depois implementos o restante
endmodule

module ImediatoGenerator (
  input  [31:0] OPCODE,
  output [31:0] out_2
);

  wire and_1_out, and_2_out, and_3_out, and_5_out, and_6_out, S0, S1, S2;
  wire [31:0] bit_extender_1_out, bit_extender_2_out, bit_extender_3_out, bit_extender_4_out;

  // Probe on OPCODE[6:0]
  and and_1 (and_1_out, OPCODE[0], OPCODE[1], OPCODE[2], ~OPCODE[4], OPCODE[5], OPCODE[6]);  // AND_Gate
  and and_2 (and_2_out, OPCODE[0], OPCODE[1], ~OPCODE[2], ~OPCODE[3], OPCODE[5], OPCODE[6]);  // AND_Gate
  and and_3 (and_3_out, OPCODE[0], OPCODE[1], ~OPCODE[2], ~OPCODE[3], ~OPCODE[5], ~OPCODE[6]);  // AND_Gate
  and and_4 (S1, OPCODE[0], OPCODE[1], ~OPCODE[2], ~OPCODE[4], ~OPCODE[3], OPCODE[5]);  // AND_Gate
  and and_5 (and_5_out, OPCODE[0], OPCODE[1], OPCODE[2], OPCODE[3], ~OPCODE[4], OPCODE[5], OPCODE[6]);  // AND_Gate
  and and_6 (and_6_out, OPCODE[0], OPCODE[1], OPCODE[2], ~OPCODE[3], OPCODE[4], OPCODE[5], ~OPCODE[6]);  // AND_Gate
  or or_1 (S2, and_1_out, and_2_out, and_3_out);
  or or_2 (S0, and_5_out, and_6_out);
  // Probe on {S0, S1, S2}
  assign bit_extender_1_out = {{20{OPCODE[31]}}, OPCODE[31:20]};  // Bit_Extender bit_extender_1
  // Probe on bit_extender_1_out
  assign bit_extender_2_out = {{20{OPCODE[31]}}, {OPCODE[31:25], OPCODE[11:7]}};  // Bit_Extender bit_extender_2
  assign bit_extender_3_out = {{19{OPCODE[31]}}, {OPCODE[31], OPCODE[7], OPCODE[30:25], OPCODE[11:8], 1'b0}};  // Bit_Extender bit_extender_3
  // Probe on bit_extender_3_out
  // Probe on {OPCODE[31:12], {12{1'b0}}}
  // Probe on bit_extender_2_out
  // Probe on {OPCODE[31], OPCODE[19:12], OPCODE[20], OPCODE[30:21], 1'b0}
  assign bit_extender_4_out = {{11{OPCODE[31]}}, {OPCODE[31], OPCODE[19:12], OPCODE[20], OPCODE[30:21], 1'b0}};  // Bit_Extender bit_extender_4
  Multiplexer #(.select(3), .width(32)) multiplexer_1 (
    .in1(bit_extender_1_out), .in2(bit_extender_2_out), .in3(bit_extender_3_out),
    .in4({OPCODE[31:12], {12{1'b0}}}), .in5(bit_extender_4_out), .out(out_2), .sel({S0, S1, S2}));  // open: in0, in6, in7
  // Probe on out_2

  // Other names for the same wires on the sheet: A = OPCODE[0]; B = OPCODE[1]; C = OPCODE[2]; D = OPCODE[3];
  //   E = OPCODE[4]; F = OPCODE[5]; G = OPCODE[6]; seletor[2:0] = {S0, S1, S2}

  // Notes on the sheet:
  //   OPCODE: initial=0x7a17d
  //   separa os bits em um circ combinacional e gera 3 bits de controle para o mux dependendo do OPCODE
  //   tipo S
  //   tipo U
  //   tipo J
  //   tipo I
  //   tipo B
endmodule

module UnitControl (
  input  [6:0] in_1,
  output [8:0] out_2
);

  wire comparator_1_eq, comparator_2_eq, comparator_3_eq, comparator_4_eq;
  wire [2:0] multiplexer_1_out, multiplexer_2_out, multiplexer_3_out, multiplexer_4_out, or_1_out;

  Comparator #(.width(7)) comparator_1 (.a(in_1), .b(7'b0000011), .eq(comparator_1_eq));  // open: gt, lt
  Comparator #(.width(7)) comparator_2 (.a(in_1), .b(7'b0100011), .eq(comparator_2_eq));  // open: gt, lt
  Comparator #(.width(7)) comparator_3 (.a(in_1), .b(7'b0110011), .eq(comparator_3_eq));  // open: gt, lt
  Comparator #(.width(7)) comparator_4 (.a(in_1), .b(7'b1100011), .eq(comparator_4_eq));  // open: gt, lt
  Multiplexer #(.width(3)) multiplexer_1 (.in0(3'b000), .in1(3'b001), .out(multiplexer_1_out), .sel(comparator_1_eq));
  Multiplexer #(.width(3)) multiplexer_2 (.in0(3'b000), .in1(3'b010), .out(multiplexer_2_out), .sel(comparator_2_eq));
  Multiplexer #(.width(3)) multiplexer_3 (.in0(3'b000), .in1(3'b011), .out(multiplexer_3_out), .sel(comparator_3_eq));
  Multiplexer #(.width(3)) multiplexer_4 (.in0(3'b000), .in1(3'b100), .out(multiplexer_4_out), .sel(comparator_4_eq));
  assign or_1_out = multiplexer_1_out | multiplexer_2_out | multiplexer_3_out | multiplexer_4_out;  // OR_Gate or_1, 3 bits wide
  Multiplexer #(.select(3), .width(9)) multiplexer_5 (
    .in0({9{1'b0}}), .in1(9'h128), .in2(9'h70), .in3(9'h102), .in4(9'h85), .in5({9{1'b0}}), .in6({9{1'b0}}),
    .in7({9{1'b0}}), .out(out_2), .sel(or_1_out));
endmodule

module ALUOp (
  input  [1:0] in_1,
  input  [2:0] in_2,
  input  in_3,
  input  in_4,
  output [2:0] out_5
);

  wire and_1_out, comparator_1_eq, comparator_2_eq, comparator_3_eq, comparator_4_eq, comparator_5_eq,
       comparator_6_eq, comparator_7_eq, comparator_8_eq;
  wire [2:0] CS, multiplexer_1_out, multiplexer_2_out, multiplexer_3_out, multiplexer_4_out,
       multiplexer_5_out, multiplexer_6_out, multiplexer_7_out, or_1_out;

  Comparator #(.width(3)) comparator_1 (.a(in_2), .b(3'b000), .eq(comparator_1_eq));  // open: gt, lt
  Comparator #(.width(2)) comparator_2 (.a({in_4, in_3}), .b(2'b11), .eq(comparator_2_eq));  // open: gt, lt
  Comparator #(.width(3)) comparator_3 (.a(in_2), .b(3'b010), .eq(comparator_3_eq));  // open: gt, lt
  Comparator #(.width(3)) comparator_4 (.a(in_2), .b(3'b110), .eq(comparator_4_eq));  // open: gt, lt
  Comparator #(.width(3)) comparator_5 (.a(in_2), .b(3'b111), .eq(comparator_5_eq));  // open: gt, lt
  Comparator #(.width(2)) comparator_6 (.a(in_1), .b(2'b00), .eq(comparator_6_eq));  // open: gt, lt
  Comparator #(.width(2)) comparator_7 (.a(in_1), .b(2'b01), .eq(comparator_7_eq));  // open: gt, lt
  Comparator #(.width(2)) comparator_8 (.a(in_1), .b(2'b10), .eq(comparator_8_eq));  // open: gt, lt
  and and_1 (and_1_out, comparator_1_eq, comparator_2_eq);
  Multiplexer #(.width(3)) multiplexer_1 (.in0(3'b000), .in1(3'b000), .out(multiplexer_1_out), .sel(comparator_6_eq));
  Multiplexer #(.width(3)) multiplexer_2 (.in0(3'b000), .in1(3'b001), .out(multiplexer_2_out), .sel(comparator_7_eq));
  Multiplexer #(.width(3)) multiplexer_3 (.in0(3'b000), .in1(CS), .out(multiplexer_3_out), .sel(comparator_8_eq));
  Multiplexer #(.width(3)) multiplexer_4 (.in0(3'b000), .in1(3'b001), .out(multiplexer_4_out), .sel(and_1_out));
  Multiplexer #(.width(3)) multiplexer_5 (.in0(3'b000), .in1(3'b010), .out(multiplexer_5_out), .sel(comparator_3_eq));
  Multiplexer #(.width(3)) multiplexer_6 (.in0(3'b000), .in1(3'b011), .out(multiplexer_6_out), .sel(comparator_4_eq));
  Multiplexer #(.width(3)) multiplexer_7 (.in0(3'b000), .in1(3'b100), .out(multiplexer_7_out), .sel(comparator_5_eq));
  assign or_1_out = multiplexer_1_out | multiplexer_2_out | multiplexer_3_out;  // OR_Gate or_1, 3 bits wide
  assign CS = multiplexer_4_out | multiplexer_6_out | multiplexer_7_out;  // OR_Gate or_2, 3 bits wide
  Multiplexer #(.select(3), .width(3)) multiplexer_8 (
    .in0(3'b000), .in1(3'b001), .in2(3'b101), .in3(3'b011), .in4(3'b010), .in5(3'b000), .in6(3'b000),
    .in7(3'b000), .out(out_5), .sel(or_1_out));
endmodule

module REG_EX_MEM (
  input  [31:0] ALUResult_in,
  input  [31:0] WriteData_in,
  input  [4:0] rd_in,
  input  [4:0] rd_out,
  input  RegWrite_in,
  input  MemToReg_in,
  input  MemRead_in,
  input  MemWrite_in,
  output [31:0] ALUResult_out,
  output [31:0] WriteData_out,
  output RegWrite_out,
  output MemToReg_out,
  output MemRead_out,
  output MemWrite_out
);

  wire clock_1_out, clock_2_out, clock_3_out, clock_4_out, clock_5_out, clock_6_out, clock_7_out;

  Clock clock_1 (.out(clock_1_out));
  Clock clock_2 (.out(clock_2_out));
  Clock clock_3 (.out(clock_3_out));
  Register #(.width(32)) register_1 (
    .D(ALUResult_in), .en(clock_1_out), .clk(clock_1_out), .Q(ALUResult_out));  // open: clr
  Register #(.width(32)) register_2 (
    .D(WriteData_in), .en(clock_2_out), .clk(clock_2_out), .Q(WriteData_out));  // open: clr
  Register #(.width(5)) register_3 (.D(rd_in), .en(clock_3_out), .clk(clock_3_out), .Q(rd_out));  // open: clr
  Register #(.width(1)) register_4 (
    .D(RegWrite_in), .en(clock_4_out), .clk(clock_4_out), .Q(RegWrite_out));  // open: clr
  Clock clock_4 (.out(clock_4_out));
  Register #(.width(1)) register_5 (
    .D(MemToReg_in), .en(clock_5_out), .clk(clock_5_out), .Q(MemToReg_out));  // open: clr
  Clock clock_5 (.out(clock_5_out));
  Register #(.width(1)) register_6 (.D(MemRead_in), .en(clock_6_out), .clk(clock_6_out), .Q(MemRead_out));  // open: clr
  Clock clock_6 (.out(clock_6_out));
  Register #(.width(1)) register_7 (
    .D(MemWrite_in), .en(clock_7_out), .clk(clock_7_out), .Q(MemWrite_out));  // open: clr
  Clock clock_7 (.out(clock_7_out));

  // Notes on the sheet:
  //   Resultado da ALU no estagio EX
  //   Dado vindo de rs2, que sera escrito na memoria se for uma instrucao
  //   Usado no estagio WB para saber onde escrever o valor
  //   Diz se a instrucao atual deve escrever em um registrador
  //   Se 1, dado sera escrito ira vir da RAM
  //   Se 0, vira da ALU
  //   Ativa escrita na memoria
  //   Ativa leitura da memoria
endmodule

module REG_MEM_WB (
  input  [31:0] ReadData_in,
  input  [31:0] ALUResult_in,
  input  [4:0] rd_in,
  input  RegWrite_in,
  input  MemToReg_in,
  output [31:0] ReadData_out,
  output [31:0] ALUResult_out,
  output [4:0] rd_out,
  output RegWrite_out,
  output MemToReg_out
);

  wire clock_1_out, clock_2_out, clock_3_out, clock_4_out, clock_5_out;

  Clock clock_1 (.out(clock_1_out));
  Clock clock_2 (.out(clock_2_out));
  Clock clock_3 (.out(clock_3_out));
  Clock clock_4 (.out(clock_4_out));
  Clock clock_5 (.out(clock_5_out));
  Register #(.width(32)) register_1 (
    .D(ReadData_in), .en(clock_1_out), .clk(clock_1_out), .Q(ReadData_out));  // open: clr
  Register #(.width(32)) register_2 (
    .D(ALUResult_in), .en(clock_2_out), .clk(clock_2_out), .Q(ALUResult_out));  // open: clr
  Register #(.width(5)) register_3 (.D(rd_in), .en(clock_3_out), .clk(clock_3_out), .Q(rd_out));  // open: clr
  Register #(.width(1)) register_4 (
    .D(RegWrite_in), .en(clock_4_out), .clk(clock_4_out), .Q(RegWrite_out));  // open: clr
  Register #(.width(1)) register_5 (
    .D(MemToReg_in), .en(clock_5_out), .clk(clock_5_out), .Q(MemToReg_out));  // open: clr

  // Notes on the sheet:
  //   Usado quando intrucao e um load
  //   Usado quando a intrucao e do tipo aritmetica
  //   Serve para indicar onde escrever no banco de registradores
  //   Ativa escrita no banco de registradores
  //   Seleciona o dado a ser escrito no banco de registradores
endmodule
