// Digital circuit AND.dig as structural Verilog
module AND (
  input  A0,
  input  A1,
  input  A2,
  input  A3,
  input  A4,
  input  A5,
  input  A6,
  input  A7,
  input  B0,
  input  B1,
  input  B2,
  input  B3,
  input  B4,
  input  B5,
  input  B6,
  input  B7,
  output out_0,
  output out_1,
  output out_2,
  output out_3,
  output out_4,
  output out_5,
  output out_6,
  output out_7
);

  and and_1 (out_0, A0, B0);
  and and_2 (out_1, A1, B1);
  and and_3 (out_2, A2, B2);
  and and_4 (out_3, A3, B3);
  and and_5 (out_4, A4, B4);
  and and_6 (out_5, A5, B5);
  and and_7 (out_6, A6, B6);
  and and_8 (out_7, A7, B7);
endmodule
