// Digital circuit Adder.dig as structural Verilog
module Adder (
  input  A,
  input  B,
  input  C_in,
  output S,
  output C_out
);

  wire nand_1_out, nand_2_out, nand_3_out, nand_4_out, nand_5_out, nand_6_out, nand_7_out;

  nand nand_1 (nand_1_out, A, B);
  nand nand_2 (nand_2_out, A, nand_1_out);
  nand nand_3 (nand_3_out, nand_1_out, B);
  nand nand_4 (nand_4_out, nand_2_out, nand_3_out);
  nand nand_5 (nand_5_out, nand_4_out, C_in);
  nand nand_6 (nand_6_out, nand_4_out, nand_5_out);
  nand nand_7 (nand_7_out, nand_5_out, C_in);
  nand nand_8 (S, nand_6_out, nand_7_out);
  nand nand_9 (C_out, nand_5_out, nand_1_out);
endmodule
