// Digital circuit Somador 8_bit.dig as structural Verilog
module Somador_8_bit (
  input  A0,
  input  A1,
  input  A2,
  input  A3,
  input  A4,
  input  A5,
  input  A6,
  input  A7,
  input  B0,
  input  B1,
  input  B2,
  input  B3,
  input  B4,
  input  B5,
  input  B6,
  input  B7,
  output S0,
  output S1,
  output S2,
  output S3,
  output S4,
  output S5,
  output S6,
  output S7,
  output Overflow
);

  wire adder_1_c_out, adder_2_c_out, adder_3_c_out, adder_4_c_out, adder_5_c_out, adder_6_c_out,
       adder_7_c_out;

  Adder adder_1 (.A(A0), .B(B0), .C_in(1'b0), .S(S0), .C_out(adder_1_c_out));
  Adder adder_2 (.A(A1), .B(B1), .C_in(adder_1_c_out), .S(S1), .C_out(adder_2_c_out));
  Adder adder_3 (.A(A2), .B(B2), .C_in(adder_2_c_out), .S(S2), .C_out(adder_3_c_out));
  Adder adder_4 (.A(A3), .B(B3), .C_in(adder_3_c_out), .S(S3), .C_out(adder_4_c_out));
  Adder adder_5 (.A(A4), .B(B4), .C_in(adder_4_c_out), .S(S4), .C_out(adder_5_c_out));
  Adder adder_6 (.A(A5), .B(B5), .C_in(adder_5_c_out), .S(S5), .C_out(adder_6_c_out));
  Adder adder_7 (.A(A6), .B(B6), .C_in(adder_6_c_out), .S(S6), .C_out(adder_7_c_out));
  Adder adder_8 (.A(A7), .B(B7), .C_in(adder_7_c_out), .S(S7), .C_out(Overflow));
endmodule
