// Digital circuit Subtrator8_bit.dig as structural Verilog
module Subtrator8_bit (
  input  A0,
  input  A1,
  input  A2,
  input  A3,
  input  A4,
  input  A5,
  input  A6,
  input  A7,
  input  B0,
  input  B1,
  input  B2,
  input  B3,
  input  B4,
  input  B5,
  input  B6,
  input  B7,
  output S0,
  output S1,
  output S2,
  output S3,
  output S4,
  output S5,
  output S6,
  output S7,
  output Overflow
);

  wire adder_1_c_out, adder_2_c_out, adder_3_c_out, adder_4_c_out, adder_5_c_out, adder_6_c_out,
       adder_7_c_out, not_1_out, not_2_out, not_3_out, not_4_out, not_5_out, not_6_out, not_7_out, not_8_out;

  not not_1 (not_1_out, B0);
  not not_2 (not_2_out, B1);
  not not_3 (not_3_out, B2);
  not not_4 (not_4_out, B3);
  not not_5 (not_5_out, B4);
  not not_6 (not_6_out, B5);
  not not_7 (not_7_out, B6);
  not not_8 (not_8_out, B7);
  Adder adder_1 (.A(A0), .B(not_1_out), .C_in(1'b1), .S(S0), .C_out(adder_1_c_out));
  Adder adder_2 (.A(A1), .B(not_2_out), .C_in(adder_1_c_out), .S(S1), .C_out(adder_2_c_out));
  Adder adder_3 (.A(A2), .B(not_3_out), .C_in(adder_2_c_out), .S(S2), .C_out(adder_3_c_out));
  Adder adder_4 (.A(A3), .B(not_4_out), .C_in(adder_3_c_out), .S(S3), .C_out(adder_4_c_out));
  Adder adder_5 (.A(A4), .B(not_5_out), .C_in(adder_4_c_out), .S(S4), .C_out(adder_5_c_out));
  Adder adder_6 (.A(A5), .B(not_6_out), .C_in(adder_5_c_out), .S(S5), .C_out(adder_6_c_out));
  Adder adder_7 (.A(A6), .B(not_7_out), .C_in(adder_6_c_out), .S(S6), .C_out(adder_7_c_out));
  Adder adder_8 (.A(A7), .B(not_8_out), .C_in(adder_7_c_out), .S(S7), .C_out(Overflow));
endmodule
