// Digital circuit ULA.dig as structural Verilog
module ULA (
  input  data_A0,
  input  data_A1,
  input  data_A2,
  input  data_A3,
  input  data_A4,
  input  data_A5,
  input  data_A6,
  input  data_A7,
  input  data_B0,
  input  data_B1,
  input  data_B2,
  input  data_B3,
  input  data_B4,
  input  data_B5,
  input  data_B6,
  input  data_B7,
  input  sel_b0,
  input  sel_b1,
  input  sel_b2
);

  AND and_1 ();  // open: A0, A1, A2, A3, A4, A5, A6, A7, B0, B1, B2, B3, B4, B5, B6, B7, out_0, out_1, out_2, out_3, out_4, out_5, out_6, out_7
  OR or_1 ();  // open: A0, A1, A2, A3, A4, A5, A6, A7, B0, B1, B2, B3, B4, B5, B6, B7, out_0, out_1, out_2, out_3, out_4, out_5, out_6, out_7
endmodule
