// Digital circuit Banco de Registradores.dig as structural Verilog
module Banco_de_Registradores (
  input  rd_0,
  input  rd_1,
  input  rd_2,
  input  rd_3,
  input  rd_4,
  input  rd_5,
  input  rd_6,
  input  rd_7,
  input  enable,
  input  clk,
  input  FE0,
  input  FE1,
  input  FE2,
  input  Rs1_B0,
  input  Rs1_B1,
  input  Rs1_B2,
  input  Rs2_B0,
  input  Rs2_B1,
  input  Rs2_B2,
  output Rs1_S0,
  output Rs2_S0,
  output Rs1_S1,
  output Rs1_S2,
  output Rs1_S3,
  output Rs1_S4,
  output Rs1_S5,
  output Rs1_S6,
  output Rs1_S7,
  output Rs2_S1,
  output Rs2_S2,
  output Rs2_S3,
  output Rs2_S4,
  output Rs2_S5,
  output Rs2_S6,
  output Rs2_S7
);

  wire demux_1_b1, demux_1_b2, demux_1_b3, demux_1_b4, demux_1_b5, demux_1_b6, demux_1_b7, Reg1_out_0,
       Reg1_out_1, Reg1_out_2, Reg1_out_3, Reg1_out_4, Reg1_out_5, Reg1_out_6, Reg1_out_7, Reg2_out_0,
       Reg2_out_1, Reg2_out_2, Reg2_out_3, Reg2_out_4, Reg2_out_5, Reg2_out_6, Reg2_out_7, reg3_out_0,
       reg3_out_1, reg3_out_2, reg3_out_3, reg3_out_4, reg3_out_5, reg3_out_6, reg3_out_7, reg4_out_0,
       reg4_out_1, reg4_out_2, reg4_out_3, reg4_out_4, reg4_out_5, reg4_out_6, reg4_out_7, reg5_out_0,
       reg5_out_1, reg5_out_2, reg5_out_3, reg5_out_4, reg5_out_5, reg5_out_6, reg5_out_7, reg6_out_0,
       reg6_out_1, reg6_out_2, reg6_out_3, reg6_out_4, reg6_out_5, reg6_out_6, reg6_out_7, Reg7_out_0,
       Reg7_out_1, Reg7_out_2, Reg7_out_3, Reg7_out_4, Reg7_out_5, Reg7_out_6, Reg7_out_7;

  Demux demux_1 (
    .Enable(enable), .B1(demux_1_b1), .B2(demux_1_b2), .B3(demux_1_b3), .B4(demux_1_b4), .B5(demux_1_b5),
    .B6(demux_1_b6), .B7(demux_1_b7), .S2(FE2), .S1(FE1), .S0(FE0));  // open: B0
  Registrador Reg1 (
    .in_0(rd_0), .in_1(rd_1), .in_2(rd_2), .in_3(rd_3), .in_4(rd_4), .in_5(rd_5), .in_6(rd_6), .in_7(rd_7),
    .clk(clk), .Enable(demux_1_b1), .out_0(Reg1_out_0), .out_1(Reg1_out_1), .out_2(Reg1_out_2),
    .out_3(Reg1_out_3), .out_4(Reg1_out_4), .out_5(Reg1_out_5), .out_6(Reg1_out_6), .out_7(Reg1_out_7));
  Registrador Reg2 (
    .in_0(rd_0), .in_1(rd_1), .in_2(rd_2), .in_3(rd_3), .in_4(rd_4), .in_5(rd_5), .in_6(rd_6), .in_7(rd_7),
    .clk(clk), .Enable(demux_1_b2), .out_0(Reg2_out_0), .out_1(Reg2_out_1), .out_2(Reg2_out_2),
    .out_3(Reg2_out_3), .out_4(Reg2_out_4), .out_5(Reg2_out_5), .out_6(Reg2_out_6), .out_7(Reg2_out_7));
  Registrador reg3 (
    .in_0(rd_0), .in_1(rd_1), .in_2(rd_2), .in_3(rd_3), .in_4(rd_4), .in_5(rd_5), .in_6(rd_6), .in_7(rd_7),
    .clk(clk), .Enable(demux_1_b3), .out_0(reg3_out_0), .out_1(reg3_out_1), .out_2(reg3_out_2),
    .out_3(reg3_out_3), .out_4(reg3_out_4), .out_5(reg3_out_5), .out_6(reg3_out_6), .out_7(reg3_out_7));
  Registrador reg4 (
    .in_0(rd_0), .in_1(rd_1), .in_2(rd_2), .in_3(rd_3), .in_4(rd_4), .in_5(rd_5), .in_6(rd_6), .in_7(rd_7),
    .clk(clk), .Enable(demux_1_b4), .out_0(reg4_out_0), .out_1(reg4_out_1), .out_2(reg4_out_2),
    .out_3(reg4_out_3), .out_4(reg4_out_4), .out_5(reg4_out_5), .out_6(reg4_out_6), .out_7(reg4_out_7));
  Registrador reg5 (
    .in_0(rd_0), .in_1(rd_1), .in_2(rd_2), .in_3(rd_3), .in_4(rd_4), .in_5(rd_5), .in_6(rd_6), .in_7(rd_7),
    .clk(clk), .Enable(demux_1_b5), .out_0(reg5_out_0), .out_1(reg5_out_1), .out_2(reg5_out_2),
    .out_3(reg5_out_3), .out_4(reg5_out_4), .out_5(reg5_out_5), .out_6(reg5_out_6), .out_7(reg5_out_7));
  Registrador reg6 (
    .in_0(rd_0), .in_1(rd_1), .in_2(rd_2), .in_3(rd_3), .in_4(rd_4), .in_5(rd_5), .in_6(rd_6), .in_7(rd_7),
    .clk(clk), .Enable(demux_1_b6), .out_0(reg6_out_0), .out_1(reg6_out_1), .out_2(reg6_out_2),
    .out_3(reg6_out_3), .out_4(reg6_out_4), .out_5(reg6_out_5), .out_6(reg6_out_6), .out_7(reg6_out_7));
  Registrador Reg7 (
    .in_0(rd_0), .in_1(rd_1), .in_2(rd_2), .in_3(rd_3), .in_4(rd_4), .in_5(rd_5), .in_6(rd_6), .in_7(rd_7),
    .clk(clk), .Enable(demux_1_b7), .out_0(Reg7_out_0), .out_1(Reg7_out_1), .out_2(Reg7_out_2),
    .out_3(Reg7_out_3), .out_4(Reg7_out_4), .out_5(Reg7_out_5), .out_6(Reg7_out_6), .out_7(Reg7_out_7));
  mux8bits_8x1 mux8bits_8x1_1 (
    .A0(1'b0), .A1(1'b0), .A2(1'b0), .A3(1'b0), .A4(1'b0), .A5(1'b0), .A6(1'b0), .A7(1'b0), .B0(Reg1_out_0),
    .B1(Reg1_out_1), .B2(Reg1_out_2), .B3(Reg1_out_3), .B4(Reg1_out_4), .B5(Reg1_out_5), .B6(Reg1_out_6),
    .B7(Reg1_out_7), .C0(Reg2_out_0), .C1(Reg2_out_1), .C2(Reg2_out_2), .C3(Reg2_out_3), .C4(Reg2_out_4),
    .C5(Reg2_out_5), .C6(Reg2_out_6), .C7(Reg2_out_7), .D0(reg3_out_0), .D1(reg3_out_1), .D2(reg3_out_2),
    .D3(reg3_out_3), .D4(reg3_out_4), .D5(reg3_out_5), .D6(reg3_out_6), .D7(reg3_out_7), .E0(reg4_out_0),
    .E1(reg4_out_1), .E2(reg4_out_2), .E3(reg4_out_3), .E4(reg4_out_4), .E5(reg4_out_5), .E6(reg4_out_6),
    .E7(reg4_out_7), .F0(reg5_out_0), .F1(reg5_out_1), .F2(reg5_out_2), .F3(reg5_out_3), .F4(reg5_out_4),
    .F5(reg5_out_5), .F6(reg5_out_6), .F7(reg5_out_7), .G0(reg6_out_0), .G1(reg6_out_1), .G2(reg6_out_2),
    .G3(reg6_out_3), .G4(reg6_out_4), .G5(reg6_out_5), .G6(reg6_out_6), .G7(reg6_out_7), .H0(Reg7_out_0),
    .H1(Reg7_out_1), .H2(Reg7_out_2), .H3(Reg7_out_3), .H4(Reg7_out_4), .H5(Reg7_out_5), .H6(Reg7_out_6),
    .H7(Reg7_out_7), .Slc_2(Rs1_B2), .Slc_1(Rs1_B1), .Slc_0(Rs1_B0), .S0(Rs1_S0), .S1(Rs1_S1), .S2(Rs1_S2),
    .S3(Rs1_S3), .S4(Rs1_S4), .S5(Rs1_S5), .S6(Rs1_S6), .S7(Rs1_S7));
  mux8bits_8x1 mux8bits_8x1_2 (
    .A0(1'b0), .A1(1'b0), .A2(1'b0), .A3(1'b0), .A4(1'b0), .A5(1'b0), .A6(1'b0), .A7(1'b0), .B0(Reg1_out_0),
    .B1(Reg1_out_1), .B2(Reg1_out_2), .B3(Reg1_out_3), .B4(Reg1_out_4), .B5(Reg1_out_5), .B6(Reg1_out_6),
    .B7(Reg1_out_7), .C0(Reg2_out_0), .C1(Reg2_out_1), .C2(Reg2_out_2), .C3(Reg2_out_3), .C4(Reg2_out_4),
    .C5(Reg2_out_5), .C6(Reg2_out_6), .C7(Reg2_out_7), .D0(reg3_out_0), .D1(reg3_out_1), .D2(reg3_out_2),
    .D3(reg3_out_3), .D4(reg3_out_4), .D5(reg3_out_5), .D6(reg3_out_6), .D7(reg3_out_7), .E0(reg4_out_0),
    .E1(reg4_out_1), .E2(reg4_out_2), .E3(reg4_out_3), .E4(reg4_out_4), .E5(reg4_out_5), .E6(reg4_out_6),
    .E7(reg4_out_7), .F0(reg5_out_0), .F1(reg5_out_1), .F2(reg5_out_2), .F3(reg5_out_3), .F4(reg5_out_4),
    .F5(reg5_out_5), .F6(reg5_out_6), .F7(reg5_out_7), .G0(reg6_out_0), .G1(reg6_out_1), .G2(reg6_out_2),
    .G3(reg6_out_3), .G4(reg6_out_4), .G5(reg6_out_5), .G6(reg6_out_6), .G7(reg6_out_7), .H0(Reg7_out_0),
    .H1(Reg7_out_1), .H2(Reg7_out_2), .H3(Reg7_out_3), .H4(Reg7_out_4), .H5(Reg7_out_5), .H6(Reg7_out_6),
    .H7(Reg7_out_7), .Slc_2(Rs2_B2), .Slc_1(Rs2_B1), .Slc_0(Rs2_B0), .S0(Rs2_S0), .S1(Rs2_S1), .S2(Rs2_S2),
    .S3(Rs2_S3), .S4(Rs2_S4), .S5(Rs2_S5), .S6(Rs2_S6), .S7(Rs2_S7));
endmodule
