// Digital circuit Demux.dig as structural Verilog
module Demux (
  input  S2,
  input  S1,
  input  S0,
  input  Enable,
  output B0,
  output B1,
  output B2,
  output B3,
  output B4,
  output B5,
  output B6,
  output B7
);

  wire not_1_out, not_2_out, not_3_out;

  not not_1 (not_1_out, S2);
  not not_2 (not_2_out, S1);
  not not_3 (not_3_out, S0);
  and and_1 (B0, not_3_out, not_2_out, not_1_out, Enable);
  and and_2 (B1, S0, not_2_out, not_1_out, Enable);
  and and_3 (B2, not_3_out, S1, not_1_out, Enable);
  and and_4 (B3, S0, S1, not_1_out, Enable);
  and and_5 (B4, not_3_out, not_2_out, S2, Enable);
  and and_6 (B5, S0, not_2_out, S2, Enable);
  and and_7 (B6, not_3_out, S1, S2, Enable);
  and and_8 (B7, S0, S1, S2, Enable);
endmodule
