// Digital circuit Registrador.dig as structural Verilog
module Registrador (
  input  in_0,
  input  in_1,
  input  in_2,
  input  in_3,
  input  in_4,
  input  in_5,
  input  in_6,
  input  in_7,
  input  clk,
  input  Enable,
  output out_0,
  output out_1,
  output out_2,
  output out_3,
  output out_4,
  output out_5,
  output out_6,
  output out_7
);

  wire and_1_out;

  and and_1 (and_1_out, clk, Enable);
  flip_flop_d flip_flop_d_1 (.D(in_0), .clk(and_1_out), .Q(out_0));
  flip_flop_d flip_flop_d_2 (.D(in_1), .clk(and_1_out), .Q(out_1));
  flip_flop_d flip_flop_d_3 (.D(in_2), .clk(and_1_out), .Q(out_2));
  flip_flop_d flip_flop_d_4 (.D(in_3), .clk(and_1_out), .Q(out_3));
  flip_flop_d flip_flop_d_5 (.D(in_4), .clk(and_1_out), .Q(out_4));
  flip_flop_d flip_flop_d_6 (.D(in_5), .clk(and_1_out), .Q(out_5));
  flip_flop_d flip_flop_d_7 (.D(in_6), .clk(and_1_out), .Q(out_6));
  flip_flop_d flip_flop_d_8 (.D(in_7), .clk(and_1_out), .Q(out_7));
endmodule
