// Digital circuit Demux 1x4.dig as structural Verilog
module Demux_1x4 (
  input  Enable,
  input  S0,
  input  S1,
  output B0,
  output B1,
  output B2,
  output B3
);

  wire not_1_out, not_2_out;

  not not_1 (not_1_out, S1);
  not not_2 (not_2_out, S0);
  and and_1 (B0, not_2_out, not_1_out, Enable);
  and and_2 (B1, S0, not_1_out, Enable);
  and and_3 (B2, not_2_out, S1, Enable);
  and and_4 (B3, S0, S1, Enable);
endmodule
