// Digital circuit mux 4x1.dig as structural Verilog
module mux_4x1 (
  input  B0,
  input  B1,
  input  B2,
  input  B3,
  input  F0,
  input  F1,
  output S
);

  wire mux_2x1_1_s, mux_2x1_2_s;

  mux_2x1 mux_2x1_1 (._0(B0), ._1(B1), .S(mux_2x1_1_s));  // open: F
  mux_2x1 mux_2x1_2 (._0(B2), ._1(B3), .S(mux_2x1_2_s));  // open: F
  mux_2x1 mux_2x1_3 (._0(mux_2x1_1_s), ._1(mux_2x1_2_s), .S(S));  // open: F
endmodule
