// Digital circuit mux 8x1.dig as structural Verilog
module mux_8x1 (
  input  B0,
  input  B1,
  input  B2,
  input  B3,
  input  B4,
  input  B5,
  input  B6,
  input  B7,
  input  F0,
  input  F1,
  input  F2,
  output S
);

  wire mux_4x1_1_s, mux_4x1_2_s;

  mux_4x1 mux_4x1_1 (.B0(B0), .B1(B1), .B2(B2), .B3(B3), .F1(F1), .F0(F0), .S(mux_4x1_1_s));
  mux_4x1 mux_4x1_2 (.B0(B4), .B1(B5), .B2(B6), .B3(B7), .F1(F1), .F0(F0), .S(mux_4x1_2_s));
  mux_2x1 mux_2x1_1 (._0(mux_4x1_1_s), ._1(mux_4x1_2_s), .S(S));  // open: F
endmodule
