// Digital circuit mux8bits 2x1.dig as structural Verilog
module mux8bits_2x1 (
  input  A0,
  input  F,
  input  A1,
  input  A2,
  input  A3,
  input  A4,
  input  A5,
  input  A6,
  input  A7,
  input  B0,
  input  B1,
  input  B2,
  input  B3,
  input  B4,
  input  B5,
  input  B6,
  input  B7,
  output S0,
  output S1,
  output S2,
  output S3,
  output S4,
  output S5,
  output S6,
  output S7
);

  wire and8bits_1_s0, and8bits_1_s1, and8bits_1_s2, and8bits_1_s3, and8bits_1_s4, and8bits_1_s5,
       and8bits_1_s6, and8bits_1_s7, and8bits_2_s0, and8bits_2_s1, and8bits_2_s2, and8bits_2_s3,
       and8bits_2_s4, and8bits_2_s5, and8bits_2_s6, and8bits_2_s7, not_1_out;

  not not_1 (not_1_out, F);
  AND8bits and8bits_1 (
    .S0(and8bits_1_s0), .S1(and8bits_1_s1), .S2(and8bits_1_s2), .S3(and8bits_1_s3), .S4(and8bits_1_s4),
    .S5(and8bits_1_s5), .S6(and8bits_1_s6), .S7(and8bits_1_s7), .A0(A0), .A1(A1), .A2(A2), .A3(A3), .A4(A4),
    .A5(A5), .A6(A6), .A7(A7), .B0(not_1_out), .B1(not_1_out), .B2(not_1_out), .B3(not_1_out),
    .B4(not_1_out), .B5(not_1_out), .B6(not_1_out), .B7(not_1_out));
  AND8bits and8bits_2 (
    .S0(and8bits_2_s0), .S1(and8bits_2_s1), .S2(and8bits_2_s2), .S3(and8bits_2_s3), .S4(and8bits_2_s4),
    .S5(and8bits_2_s5), .S6(and8bits_2_s6), .S7(and8bits_2_s7), .A0(F), .A1(F), .A2(F), .A3(F), .A4(F),
    .A5(F), .A6(F), .A7(F), .B0(B0), .B1(B1), .B2(B2), .B3(B3), .B4(B4), .B5(B5), .B6(B6), .B7(B7));
  OR8bits or8bits_1 (
    .A0(and8bits_1_s0), .A1(and8bits_1_s1), .A2(and8bits_1_s2), .A3(and8bits_1_s3), .A4(and8bits_1_s4),
    .A5(and8bits_1_s5), .A6(and8bits_1_s6), .A7(and8bits_1_s7), .B0(and8bits_2_s0), .B1(and8bits_2_s1),
    .B2(and8bits_2_s2), .B3(and8bits_2_s3), .B4(and8bits_2_s4), .B5(and8bits_2_s5), .B6(and8bits_2_s6),
    .B7(and8bits_2_s7), .S0(S0), .S1(S1), .S2(S2), .S3(S3), .S4(S4), .S5(S5), .S6(S6), .S7(S7));
endmodule
