// Digital circuit mux8bits 4x1.dig as structural Verilog
module mux8bits_4x1 (
  input  In_A0,
  input  In_A1,
  input  In_A2,
  input  In_A3,
  input  In_A4,
  input  In_A5,
  input  In_A6,
  input  In_A7,
  input  In_B0,
  input  In_B1,
  input  In_B2,
  input  In_B3,
  input  In_B4,
  input  In_B5,
  input  In_B6,
  input  In_B7,
  input  In_C0,
  input  In_C1,
  input  In_C2,
  input  In_C3,
  input  In_C4,
  input  In_C5,
  input  In_C6,
  input  In_C7,
  input  In_D1,
  input  In_D2,
  input  In_D3,
  input  In_D4,
  input  In_D5,
  input  In_D6,
  input  In_D7,
  input  F1,
  input  F0,
  input  In_D0,
  output S0,
  output S1,
  output S2,
  output S3,
  output S4,
  output S5,
  output S6,
  output S7
);

  wire mux8bits_2x1_1_s0, mux8bits_2x1_1_s1, mux8bits_2x1_1_s2, mux8bits_2x1_1_s3, mux8bits_2x1_1_s4,
       mux8bits_2x1_1_s5, mux8bits_2x1_1_s6, mux8bits_2x1_1_s7, mux8bits_2x1_2_s0, mux8bits_2x1_2_s1,
       mux8bits_2x1_2_s2, mux8bits_2x1_2_s3, mux8bits_2x1_2_s4, mux8bits_2x1_2_s5, mux8bits_2x1_2_s6,
       mux8bits_2x1_2_s7;

  mux8bits_2x1 mux8bits_2x1_1 (
    .A0(In_A0), .A1(In_A1), .A2(In_A2), .A3(In_A3), .A4(In_A4), .A5(In_A5), .A6(In_A6), .A7(In_A7),
    .B0(In_B0), .B1(In_B1), .B2(In_B2), .B3(In_B3), .B4(In_B4), .B5(In_B5), .B6(In_B6), .B7(In_B7), .F(F0),
    .S0(mux8bits_2x1_1_s0), .S1(mux8bits_2x1_1_s1), .S2(mux8bits_2x1_1_s2), .S3(mux8bits_2x1_1_s3),
    .S4(mux8bits_2x1_1_s4), .S5(mux8bits_2x1_1_s5), .S6(mux8bits_2x1_1_s6), .S7(mux8bits_2x1_1_s7));
  mux8bits_2x1 mux8bits_2x1_2 (
    .A0(In_C0), .A1(In_C1), .A2(In_C2), .A3(In_C3), .A4(In_C4), .A5(In_C5), .A6(In_C6), .A7(In_C7),
    .B0(In_D0), .B1(In_D1), .B2(In_D2), .B3(In_D3), .B4(In_D4), .B5(In_D5), .B6(In_D6), .B7(In_D7), .F(F0),
    .S0(mux8bits_2x1_2_s0), .S1(mux8bits_2x1_2_s1), .S2(mux8bits_2x1_2_s2), .S3(mux8bits_2x1_2_s3),
    .S4(mux8bits_2x1_2_s4), .S5(mux8bits_2x1_2_s5), .S6(mux8bits_2x1_2_s6), .S7(mux8bits_2x1_2_s7));
  mux8bits_2x1 mux8bits_2x1_3 (
    .A0(mux8bits_2x1_1_s0), .A1(mux8bits_2x1_1_s1), .A2(mux8bits_2x1_1_s2), .A3(mux8bits_2x1_1_s3),
    .A4(mux8bits_2x1_1_s4), .A5(mux8bits_2x1_1_s5), .A6(mux8bits_2x1_1_s6), .A7(mux8bits_2x1_1_s7),
    .B0(mux8bits_2x1_2_s0), .B1(mux8bits_2x1_2_s1), .B2(mux8bits_2x1_2_s2), .B3(mux8bits_2x1_2_s3),
    .B4(mux8bits_2x1_2_s4), .B5(mux8bits_2x1_2_s5), .B6(mux8bits_2x1_2_s6), .B7(mux8bits_2x1_2_s7), .F(F1),
    .S0(S0), .S1(S1), .S2(S2), .S3(S3), .S4(S4), .S5(S5), .S6(S6), .S7(S7));
endmodule
