// Digital circuit mux8bits 8x1.dig as structural Verilog
module mux8bits_8x1 (
  input  A0,
  input  A1,
  input  A2,
  input  A3,
  input  A4,
  input  A5,
  input  A6,
  input  A7,
  input  B0,
  input  B1,
  input  B2,
  input  B3,
  input  B4,
  input  B5,
  input  B6,
  input  B7,
  input  C0,
  input  C1,
  input  C2,
  input  C3,
  input  C4,
  input  C5,
  input  C6,
  input  C7,
  input  D0,
  input  D1,
  input  D2,
  input  D3,
  input  D4,
  input  D5,
  input  D6,
  input  D7,
  input  E0,
  input  E1,
  input  E2,
  input  E3,
  input  E4,
  input  E5,
  input  E6,
  input  E7,
  input  F0,
  input  F1,
  input  F2,
  input  F3,
  input  F4,
  input  F5,
  input  F6,
  input  F7,
  input  G0,
  input  G1,
  input  G2,
  input  G3,
  input  G4,
  input  G5,
  input  G6,
  input  G7,
  input  H0,
  input  H1,
  input  H2,
  input  H3,
  input  H4,
  input  H5,
  input  H6,
  input  H7,
  input  Slc_0,
  input  Slc_1,
  input  Slc_2,
  output S0,
  output S1,
  output S2,
  output S3,
  output S4,
  output S5,
  output S6,
  output S7
);

  wire mux8bits_4x1_1_s0, mux8bits_4x1_1_s1, mux8bits_4x1_1_s2, mux8bits_4x1_1_s3, mux8bits_4x1_1_s4,
       mux8bits_4x1_1_s5, mux8bits_4x1_1_s6, mux8bits_4x1_1_s7, mux8bits_4x1_2_s0, mux8bits_4x1_2_s1,
       mux8bits_4x1_2_s2, mux8bits_4x1_2_s3, mux8bits_4x1_2_s4, mux8bits_4x1_2_s5, mux8bits_4x1_2_s6,
       mux8bits_4x1_2_s7;

  mux8bits_4x1 mux8bits_4x1_1 (
    .In_A0(A0), .In_A1(A1), .In_A2(A2), .In_A3(A3), .In_A4(A4), .In_A5(A5), .In_A6(A6), .In_A7(A7),
    .In_B0(B0), .In_B1(B1), .In_B2(B2), .In_B3(B3), .In_B4(B4), .In_B5(B5), .In_B6(B6), .In_B7(B7),
    .In_C0(C0), .In_C1(C1), .In_C2(C2), .In_C3(C3), .In_C4(C4), .In_C5(C5), .In_C6(C6), .In_C7(C7),
    .In_D0(D0), .In_D1(D1), .In_D2(D2), .In_D3(D3), .In_D4(D4), .In_D5(D5), .In_D6(D6), .In_D7(D7),
    .F1(Slc_1), .F0(Slc_0), .S0(mux8bits_4x1_1_s0), .S1(mux8bits_4x1_1_s1), .S2(mux8bits_4x1_1_s2),
    .S3(mux8bits_4x1_1_s3), .S4(mux8bits_4x1_1_s4), .S5(mux8bits_4x1_1_s5), .S6(mux8bits_4x1_1_s6),
    .S7(mux8bits_4x1_1_s7));
  mux8bits_4x1 mux8bits_4x1_2 (
    .In_A0(E0), .In_A1(E1), .In_A2(E2), .In_A3(E3), .In_A4(E4), .In_A5(E5), .In_A6(E6), .In_A7(E7),
    .In_B0(F0), .In_B1(F1), .In_B2(F2), .In_B3(F3), .In_B4(F4), .In_B5(F5), .In_B6(F6), .In_B7(F7),
    .In_C0(G0), .In_C1(G1), .In_C2(G2), .In_C3(G3), .In_C4(G4), .In_C5(G5), .In_C6(G6), .In_C7(G7),
    .In_D0(H0), .In_D1(H1), .In_D2(H2), .In_D3(H3), .In_D4(H4), .In_D5(H5), .In_D6(H6), .In_D7(H7),
    .F1(Slc_1), .F0(Slc_0), .S0(mux8bits_4x1_2_s0), .S1(mux8bits_4x1_2_s1), .S2(mux8bits_4x1_2_s2),
    .S3(mux8bits_4x1_2_s3), .S4(mux8bits_4x1_2_s4), .S5(mux8bits_4x1_2_s5), .S6(mux8bits_4x1_2_s6),
    .S7(mux8bits_4x1_2_s7));
  mux8bits_2x1 mux8bits_2x1_1 (
    .A0(mux8bits_4x1_1_s0), .A1(mux8bits_4x1_1_s1), .A2(mux8bits_4x1_1_s2), .A3(mux8bits_4x1_1_s3),
    .A4(mux8bits_4x1_1_s4), .A5(mux8bits_4x1_1_s5), .A6(mux8bits_4x1_1_s6), .A7(mux8bits_4x1_1_s7),
    .B0(mux8bits_4x1_2_s0), .B1(mux8bits_4x1_2_s1), .B2(mux8bits_4x1_2_s2), .B3(mux8bits_4x1_2_s3),
    .B4(mux8bits_4x1_2_s4), .B5(mux8bits_4x1_2_s5), .B6(mux8bits_4x1_2_s6), .B7(mux8bits_4x1_2_s7),
    .F(Slc_2), .S0(S0), .S1(S1), .S2(S2), .S3(S3), .S4(S4), .S5(S5), .S6(S6), .S7(S7));
endmodule
