// Digital circuit mux 2x1.dig as structural Verilog
module mux_2x1 (
  input  _0,
  input  _1,
  input  F,
  output S
);

  wire and_1_out, and_2_out;

  and and_1 (and_1_out, _0, ~F);  // And
  and and_2 (and_2_out, _1, F);
  or or_1 (S, and_1_out, and_2_out);
endmodule
